# Fritzing sketch push_btn (saved by Fritzing 0.9.3b)
breadboards: 1

parts:
  S1 = Pushbutton [package="[THT]"]
  Part1 = Arduino Mega 2560 (Rev3)
  R1 = Resistor [tolerance=±5% resistance=220 package=THT]

nets:
  N1: S1.Pin_1, S1.Pin_2
  N2: S1.Pin_3, S1.Pin_4, Part1.D10_PWM, R1.Pin_1
  N3: Part1.GND, R1.Pin_0
