# Fritzing sketch gsm (saved by Fritzing 0.9.3b)
breadboards: 1

parts:
  Part1 = Adafruit FONA 808 Breakout [part_number="Adafruit #2542"]
  Part2 = Arduino Mega 2560 (Rev3)
  U1 = 74HC595 [package="DIP16 [THT]"]  # not connected

nets:
  +5V: Part1.+5V, Part2.5V
  GND: Part1.GND, Part1.Key, Part2.GND
  N1: Part1.Reset, Part2.D4_PWM
  N2: Part1.RXD, Part2.D13_PWM
  N3: Part1.TXD, Part2.D10_PWM

custom parts:
  Adafruit FONA 808 Breakout: Cellular + GPS tracking, all in one? Oh yes! Introducing Adafruit FONA 808 MiniGSM + GPS, an all-in-one cellular phone module with that lets you add location-tracking, voice, text, SMS and data to your project in an adorable little package.
