# Fritzing sketch lcd (saved by Fritzing 0.9.3b)
breadboards: 1

parts:
  R1 = Trimmer Potentiometer [maximum_resistance=10kΩ package=THT]
  U1 = LCD-16X2 [package=lcd-16x2]
  R2 = Resistor [tolerance=±5% resistance=220 package="0603 [SMD]"]
  Part1 = Arduino Mega 2560 (Rev3)

nets:
  N1: R1.leg1, U1.VDD, R2.Pin_0
  N2: R1.wiper, U1.VO
  N3: R1.leg2, U1.VSS, U1.R_W, U1.K
  N4: U1.RS, Part1.D12_PWM
  N5: U1.E, Part1.D11_PWM
  N6: U1.DB4, Part1.D5_PWM
  N7: U1.DB5, Part1.D4_PWM
  N8: U1.DB6, Part1.D3_PWM, Part1.D6_PWM
  N9: U1.DB7, Part1.D2_PWM, Part1.D7_PWM
  N10: U1.A, R2.Pin_1
