# Fritzing sketch motor (saved by Fritzing 0.9.3b)
breadboards: 1

parts:
  Q1 = NPN-Transistor [package="TO92 [THT]"]
  R1 = Resistor [tolerance=±5% resistance=220 package=THT]
  D1 = Rectifier Diode [part_number=1N4001 package="300 mil [THT]"]
  M1 = DC Motor
  Part1 = Arduino Mega 2560 (Rev3)

nets:
  N1: Q1.E, Part1.GND
  N2: Q1.B, R1.Pin_0
  N3: Q1.C, D1.anode, M1.pin_2
  N4: R1.Pin_1, Part1.D8_PWM
  N5: D1.cathode, M1.pin_1, Part1.5V
