# Fritzing sketch tilt_sensor (saved by Fritzing 0.9.3b)
breadboards: 1

parts:
  S1 = Tilt Switch [package=THT]
  R1 = Resistor [tolerance=±5% resistance=220 package="1206 [SMD]"]
  Part1 = Arduino Mega 2560 (Rev3)

nets:
  N1: S1.Pin_1, Part1.5V
  N2: S1.Pin_2, R1.Pin_0, Part1.D9_PWM
  N3: R1.Pin_1, Part1.GND
